// Logisim project 755844-multi.circ as structural Verilog
module BR4 (
  input  [31:0] busW,
  input  reloj,
  input  reset,
  input  RegWr,
  input  [1:0] RW,
  input  [1:0] RA,
  input  [1:0] RB,
  output [31:0] busA,
  output [31:0] busB
);

  wire and_1_out, and_2_out, and_3_out, and_4_out, decoder_1_out0, decoder_1_out1, decoder_1_out2,
       decoder_1_out3;
  wire [31:0] register_1_q, register_2_q, register_3_q, register_4_q;

  Decoder #(.select(2)) decoder_1 (
    .out0(decoder_1_out0), .out1(decoder_1_out1), .out2(decoder_1_out2), .out3(decoder_1_out3), .sel(RW));  // open: en
  and and_1 (and_1_out, RegWr, decoder_1_out0);
  Register #(.width(32)) register_1 (.D(busW), .en(and_1_out), .Q(register_1_q), .clk(reloj), .clr(reset));
  and and_2 (and_2_out, RegWr, decoder_1_out1);
  Register #(.width(32)) register_2 (.D(busW), .en(and_2_out), .Q(register_2_q), .clk(reloj), .clr(reset));
  Register #(.width(32)) register_3 (.D(busW), .en(and_3_out), .Q(register_3_q), .clk(reloj), .clr(reset));
  and and_3 (and_3_out, RegWr, decoder_1_out2);
  Register #(.width(32)) register_4 (.D(busW), .en(and_4_out), .Q(register_4_q), .clk(reloj), .clr(reset));
  and and_4 (and_4_out, RegWr, decoder_1_out3);
  Multiplexer #(.select(2), .width(32), .enable("false")) multiplexer_1 (
    .in0(register_1_q), .in1(register_2_q), .in2(register_3_q), .in3(register_4_q), .out(busA), .sel(RA));
  Multiplexer #(.select(2), .width(32), .enable("false")) multiplexer_2 (
    .in0(register_1_q), .in1(register_2_q), .in2(register_3_q), .in3(register_4_q), .out(busB), .sel(RB));
endmodule

module BR32 (
  input  [4:0] RA,
  input  [4:0] RW,
  input  [4:0] RB,
  input  [31:0] busW,
  input  reset,
  input  RegWR,
  input  reloj,
  output [31:0] busA,
  output [31:0] busB
);

  wire and_1_out, and_2_out, and_3_out, and_4_out, and_5_out, and_6_out, and_7_out, and_8_out,
       decoder_1_out0, decoder_1_out1, decoder_1_out2, decoder_1_out3, decoder_1_out4, decoder_1_out5,
       decoder_1_out6, decoder_1_out7;
  wire [31:0] br4_1_busa, br4_1_busb, br4_2_busa, br4_2_busb, br4_3_busa, br4_3_busb, br4_4_busa, br4_4_busb,
       br4_5_busa, br4_5_busb, br4_6_busa, br4_6_busb, br4_7_busa, br4_7_busb, br4_8_busa, br4_8_busb;

  Decoder #(.select(3)) decoder_1 (
    .out0(decoder_1_out0), .out1(decoder_1_out1), .out2(decoder_1_out2), .out3(decoder_1_out3),
    .out4(decoder_1_out4), .out5(decoder_1_out5), .out6(decoder_1_out6), .out7(decoder_1_out7), .sel(RW[4:2]));  // open: en
  and and_1 (and_1_out, RegWR, decoder_1_out0);
  and and_2 (and_2_out, RegWR, decoder_1_out1);
  and and_3 (and_3_out, RegWR, decoder_1_out2);
  and and_4 (and_4_out, RegWR, decoder_1_out3);
  and and_5 (and_5_out, RegWR, decoder_1_out4);
  and and_6 (and_6_out, RegWR, decoder_1_out5);
  and and_7 (and_7_out, RegWR, decoder_1_out6);
  and and_8 (and_8_out, RegWR, decoder_1_out7);
  BR4 br4_1 (
    .busW(busW), .reloj(reloj), .reset(reset), .RegWr(and_1_out), .RW(RW[1:0]), .busA(br4_1_busa),
    .busB(br4_1_busb), .RA(RA[1:0]), .RB(RB[1:0]));
  BR4 br4_2 (
    .busW(busW), .reloj(reloj), .reset(reset), .RegWr(and_2_out), .RW(RW[1:0]), .busA(br4_2_busa),
    .busB(br4_2_busb), .RA(RA[1:0]), .RB(RB[1:0]));
  BR4 br4_3 (
    .busW(busW), .reloj(reloj), .reset(reset), .RegWr(and_3_out), .RW(RW[1:0]), .busA(br4_3_busa),
    .busB(br4_3_busb), .RA(RA[1:0]), .RB(RB[1:0]));
  BR4 br4_4 (
    .busW(busW), .reloj(reloj), .reset(reset), .RegWr(and_4_out), .RW(RW[1:0]), .busA(br4_4_busa),
    .busB(br4_4_busb), .RA(RA[1:0]), .RB(RB[1:0]));
  BR4 br4_5 (
    .busW(busW), .reloj(reloj), .reset(reset), .RegWr(and_5_out), .RW(RW[1:0]), .busA(br4_5_busa),
    .busB(br4_5_busb), .RA(RA[1:0]), .RB(RB[1:0]));
  BR4 br4_6 (
    .busW(busW), .reloj(reloj), .reset(reset), .RegWr(and_6_out), .RW(RW[1:0]), .busA(br4_6_busa),
    .busB(br4_6_busb), .RA(RA[1:0]), .RB(RB[1:0]));
  BR4 br4_7 (
    .busW(busW), .reloj(reloj), .reset(reset), .RegWr(and_7_out), .RW(RW[1:0]), .busA(br4_7_busa),
    .busB(br4_7_busb), .RA(RA[1:0]), .RB(RB[1:0]));
  BR4 br4_8 (
    .busW(busW), .reloj(reloj), .reset(reset), .RegWr(and_8_out), .RW(RW[1:0]), .busA(br4_8_busa),
    .busB(br4_8_busb), .RA(RA[1:0]), .RB(RB[1:0]));
  Multiplexer #(.select(3), .width(32), .enable("false")) multiplexer_1 (
    .in0(br4_1_busa), .in1(br4_2_busa), .in2(br4_3_busa), .in3(br4_4_busa), .in4(br4_5_busa),
    .in5(br4_6_busa), .in6(br4_7_busa), .in7(br4_8_busa), .out(busA), .sel(RA[4:2]));
  Multiplexer #(.select(3), .width(32), .enable("false")) multiplexer_2 (
    .in0(br4_1_busb), .in1(br4_2_busb), .in2(br4_3_busb), .in3(br4_4_busb), .in4(br4_5_busb),
    .in5(br4_6_busb), .in6(br4_7_busb), .in7(br4_8_busb), .out(busB), .sel(RB[4:2]));

  // Other names for the same wires on the sheet: RAp[1:0] = RA[1:0]; RBp[1:0] = RB[1:0]; RWp[1:0] = RW[1:0]
endmodule

module PROC (
);

  wire clock_1_out, reset_out, uc_1_mux, uc_1_pcen, uc_1_regwr;
  wire [7:0] counter_1_q;
  wire [31:0] adder_1_out, bit_extender_1_out, br32_1_busa, br32_1_busb, multiplexer_1_out, register_1_q,
       register_2_q, register_3_q, rom_1_data;

  Clock clock_1 (.out(clock_1_out));
  Button reset (.out(reset_out));
  Counter counter_1 (
    .D(counter_1_q), .count(uc_1_pcen), .Q(counter_1_q), .clk(clock_1_out), .clr(reset_out));  // open: load, carry
  ROM #(.dataWidth(32)) rom_1 (.addr(counter_1_q), .data(rom_1_data));  // open: sel
  UC uc_1 (.op(rom_1_data[31]), .reloj(clock_1_out), .PCen(uc_1_pcen), .MUX(uc_1_mux), .RegWR(uc_1_regwr));
  assign bit_extender_1_out = {{16{1'b0}}, rom_1_data[15:0]};  // Bit_Extender bit_extender_1
  BR32 br32_1 (
    .RW(rom_1_data[20:16]), .busA(br32_1_busa), .RA(rom_1_data[30:26]), .busB(br32_1_busb),
    .RB(rom_1_data[25:21]), .busW(multiplexer_1_out), .reset(reset_out), .RegWR(uc_1_regwr),
    .reloj(clock_1_out));
  Multiplexer #(.width(32), .enable("false")) multiplexer_1 (
    .in0(bit_extender_1_out), .in1(register_3_q), .out(multiplexer_1_out), .sel(uc_1_mux));
  Register #(.width(32)) register_1 (.D(br32_1_busa), .Q(register_1_q), .clk(clock_1_out));  // open: en, clr
  Register #(.width(32)) register_2 (.D(br32_1_busb), .Q(register_2_q), .clk(clock_1_out));  // open: en, clr
  Adder #(.width(32)) adder_1 (.a(register_1_q), .b(register_2_q), .out(adder_1_out));  // open: cin, cout
  Register #(.width(32)) register_3 (.D(adder_1_out), .Q(register_3_q), .clk(clock_1_out));  // open: en, clr

  // Notes on the sheet:
  //   contents of rom_1 (hex, n*v repeats v):
  //   7 10005 20005 30008 40004 50004 80260000 98460000 98660000 98860000 98a60000
endmodule

module UC (
  input  op,
  input  reloj,
  output PCen,
  output MUX,
  output RegWR
);

  wire [1:0] register_1_q;
  wire [7:3] rom_1_data;

  ROM #(.addrWidth(3)) rom_1 (.addr({op, register_1_q}), .data({rom_1_data, RegWR, MUX, PCen}));  // open: sel
  Register #(.width(2)) register_1 (.D(rom_1_data[4:3]), .Q(register_1_q), .clk(reloj));  // open: en, clr

  // Notes on the sheet:
  //   contents of rom_1 (hex, n*v repeats v):
  //   5 5 5 0 a 12 7
endmodule
