// Logisim project 755844-multi2.circ as structural Verilog
module BR4 (
  input  [31:0] busW,
  input  reloj,
  input  reset,
  input  RegWr,
  input  [1:0] RW,
  input  [1:0] RA,
  input  [1:0] RB,
  output [31:0] busA,
  output [31:0] busB
);

  wire and_1_out, and_2_out, and_3_out, and_4_out, decoder_1_out0, decoder_1_out1, decoder_1_out2,
       decoder_1_out3;
  wire [31:0] register_1_q, register_2_q, register_3_q, register_4_q;

  Decoder #(.select(2)) decoder_1 (
    .out0(decoder_1_out0), .out1(decoder_1_out1), .out2(decoder_1_out2), .out3(decoder_1_out3), .sel(RW));  // open: en
  and and_1 (and_1_out, RegWr, decoder_1_out0);
  Register #(.width(32)) register_1 (.D(busW), .en(and_1_out), .Q(register_1_q), .clk(reloj), .clr(reset));
  and and_2 (and_2_out, RegWr, decoder_1_out1);
  Register #(.width(32)) register_2 (.D(busW), .en(and_2_out), .Q(register_2_q), .clk(reloj), .clr(reset));
  Register #(.width(32)) register_3 (.D(busW), .en(and_3_out), .Q(register_3_q), .clk(reloj), .clr(reset));
  and and_3 (and_3_out, RegWr, decoder_1_out2);
  Register #(.width(32)) register_4 (.D(busW), .en(and_4_out), .Q(register_4_q), .clk(reloj), .clr(reset));
  and and_4 (and_4_out, RegWr, decoder_1_out3);
  Multiplexer #(.select(2), .width(32), .enable("false")) multiplexer_1 (
    .in0(register_1_q), .in1(register_2_q), .in2(register_3_q), .in3(register_4_q), .out(busA), .sel(RA));
  Multiplexer #(.select(2), .width(32), .enable("false")) multiplexer_2 (
    .in0(register_1_q), .in1(register_2_q), .in2(register_3_q), .in3(register_4_q), .out(busB), .sel(RB));
endmodule

module BR32 (
  input  [4:0] RA,
  input  [4:0] RW,
  input  [4:0] RB,
  input  [31:0] busW,
  input  reset,
  input  RegWR,
  input  reloj,
  output [31:0] busA,
  output [31:0] busB
);

  wire and_1_out, and_2_out, and_3_out, and_4_out, and_5_out, and_6_out, and_7_out, and_8_out,
       decoder_1_out0, decoder_1_out1, decoder_1_out2, decoder_1_out3, decoder_1_out4, decoder_1_out5,
       decoder_1_out6, decoder_1_out7;
  wire [31:0] br4_1_busa, br4_1_busb, br4_2_busa, br4_2_busb, br4_3_busa, br4_3_busb, br4_4_busa, br4_4_busb,
       br4_5_busa, br4_5_busb, br4_6_busa, br4_6_busb, br4_7_busa, br4_7_busb, br4_8_busa, br4_8_busb;

  Decoder #(.select(3)) decoder_1 (
    .out0(decoder_1_out0), .out1(decoder_1_out1), .out2(decoder_1_out2), .out3(decoder_1_out3),
    .out4(decoder_1_out4), .out5(decoder_1_out5), .out6(decoder_1_out6), .out7(decoder_1_out7), .sel(RW[4:2]));  // open: en
  and and_1 (and_1_out, RegWR, decoder_1_out0);
  and and_2 (and_2_out, RegWR, decoder_1_out1);
  and and_3 (and_3_out, RegWR, decoder_1_out2);
  and and_4 (and_4_out, RegWR, decoder_1_out3);
  and and_5 (and_5_out, RegWR, decoder_1_out4);
  and and_6 (and_6_out, RegWR, decoder_1_out5);
  and and_7 (and_7_out, RegWR, decoder_1_out6);
  and and_8 (and_8_out, RegWR, decoder_1_out7);
  BR4 br4_1 (
    .busW(busW), .reloj(reloj), .reset(reset), .RegWr(and_1_out), .RW(RW[1:0]), .busA(br4_1_busa),
    .busB(br4_1_busb), .RA(RA[1:0]), .RB(RB[1:0]));
  BR4 br4_2 (
    .busW(busW), .reloj(reloj), .reset(reset), .RegWr(and_2_out), .RW(RW[1:0]), .busA(br4_2_busa),
    .busB(br4_2_busb), .RA(RA[1:0]), .RB(RB[1:0]));
  BR4 br4_3 (
    .busW(busW), .reloj(reloj), .reset(reset), .RegWr(and_3_out), .RW(RW[1:0]), .busA(br4_3_busa),
    .busB(br4_3_busb), .RA(RA[1:0]), .RB(RB[1:0]));
  BR4 br4_4 (
    .busW(busW), .reloj(reloj), .reset(reset), .RegWr(and_4_out), .RW(RW[1:0]), .busA(br4_4_busa),
    .busB(br4_4_busb), .RA(RA[1:0]), .RB(RB[1:0]));
  BR4 br4_5 (
    .busW(busW), .reloj(reloj), .reset(reset), .RegWr(and_5_out), .RW(RW[1:0]), .busA(br4_5_busa),
    .busB(br4_5_busb), .RA(RA[1:0]), .RB(RB[1:0]));
  BR4 br4_6 (
    .busW(busW), .reloj(reloj), .reset(reset), .RegWr(and_6_out), .RW(RW[1:0]), .busA(br4_6_busa),
    .busB(br4_6_busb), .RA(RA[1:0]), .RB(RB[1:0]));
  BR4 br4_7 (
    .busW(busW), .reloj(reloj), .reset(reset), .RegWr(and_7_out), .RW(RW[1:0]), .busA(br4_7_busa),
    .busB(br4_7_busb), .RA(RA[1:0]), .RB(RB[1:0]));
  BR4 br4_8 (
    .busW(busW), .reloj(reloj), .reset(reset), .RegWr(and_8_out), .RW(RW[1:0]), .busA(br4_8_busa),
    .busB(br4_8_busb), .RA(RA[1:0]), .RB(RB[1:0]));
  Multiplexer #(.select(3), .width(32), .enable("false")) multiplexer_1 (
    .in0(br4_1_busa), .in1(br4_2_busa), .in2(br4_3_busa), .in3(br4_4_busa), .in4(br4_5_busa),
    .in5(br4_6_busa), .in6(br4_7_busa), .in7(br4_8_busa), .out(busA), .sel(RA[4:2]));
  Multiplexer #(.select(3), .width(32), .enable("false")) multiplexer_2 (
    .in0(br4_1_busb), .in1(br4_2_busb), .in2(br4_3_busb), .in3(br4_4_busb), .in4(br4_5_busb),
    .in5(br4_6_busb), .in6(br4_7_busb), .in7(br4_8_busb), .out(busB), .sel(RB[4:2]));

  // Other names for the same wires on the sheet: RAp[1:0] = RA[1:0]; RBp[1:0] = RB[1:0]; RWp[1:0] = RW[1:0]
endmodule

module PROC (
  output [4:0] out_1,
  output [31:0] out_2,
  output [4:0] out_3,
  output [4:0] out_4,
  output [31:0] out_5,
  output [1:0] out_6
);

  wire A, ALUout, and_1_out, and_2_out, B, clk, comparator_1_eq, EN, IR, MDR, multiplexer_1_out, MUX1, MUX3,
       not_1_out, or_1_out, PCcount, PCload, RegWrite, rst, signal_branch, tty_ctrl_1_clk2, tty_ctrl_1_clr,
       tty_ctrl_1_out;
  wire [2:0] OP;
  wire [4:0] multiplexer_2_out;
  wire [6:0] RAM, tty_ctrl_1_dout;
  wire [7:0] counter_1_q;
  wire [13:0] register_1_q;
  wire [15:0] ADD;
  wire [31:0] adder_1_out, br32_1_busa, multiplexer_3_out, ram_1_data, register_2_q, register_3_q,
       register_5_q, rom_1_data;
  wire [31:7] br32_1_busb;
  wire [31:16] register_4_q;

  and and_1 (and_1_out, signal_branch, comparator_1_eq);
  Counter counter_1 (
    .load(and_1_out), .D(out_5[7:0]), .count(multiplexer_1_out), .Q(counter_1_q), .clk(clk), .clr(rst));  // open: carry
  Multiplexer #(.enable("false")) multiplexer_1 (.in0(or_1_out), .in1(1'b0), .out(multiplexer_1_out), .sel(and_1_out));
  or or_1 (or_1_out, PCcount, and_2_out);
  and and_2 (and_2_out, ~OP[0], ~OP[1], ~OP[2]);  // AND_Gate
  ROM #(.dataWidth(32)) rom_1 (.addr(counter_1_q), .data(rom_1_data));  // open: sel
  tty_ctrl tty_ctrl_1 (
    .A(ADD), .E(EN), .out(tty_ctrl_1_out), .clr(tty_ctrl_1_clr), .D(RAM), .clk(clk), .Dout(tty_ctrl_1_dout),
    .clk2(tty_ctrl_1_clk2));
  TTY tty_1 (.data(tty_ctrl_1_dout), .clk(tty_ctrl_1_clk2), .we(tty_ctrl_1_out), .clr(tty_ctrl_1_clr));
  Register #(.width(32)) register_1 (
    .D(rom_1_data), .en(IR), .Q({OP, out_1, out_3, out_4, register_1_q}), .clk(clk), .clr(rst));
  Clock clock_1 (.out(clk));
  Button reset (.out(rst));
  assign out_5 = {{16{1'b0}}, {out_4, register_1_q[13:3]}};  // Bit_Extender bit_extender_1
  Multiplexer #(.width(5), .enable("false")) multiplexer_2 (
    .in0(out_3), .in1(out_4), .out(multiplexer_2_out), .sel(MUX1));
  Multiplexer #(.select(2), .width(32), .enable("false")) multiplexer_3 (
    .in0(out_5), .in1(register_5_q), .in2({register_4_q, ADD}), .out(multiplexer_3_out), .sel(out_6));  // open: in3
  BR32 br32_1 (
    .RW(multiplexer_2_out), .busA(br32_1_busa), .RA(out_1), .busB({br32_1_busb, RAM}), .RB(out_3),
    .busW(multiplexer_3_out), .reset(rst), .RegWR(RegWrite), .reloj(clk));
  UC uc_1 (
    .op(OP), .reloj(clk), .PCload(PCload), .PCcount(PCcount), .signal_branch(signal_branch), .MemWrite(EN),
    .RegWrite(RegWrite), .MUX3(MUX3), .MUX2(out_6), .MUX1(MUX1), .MDR(MDR), .ALUout(ALUout), .B(B), .A(A),
    .IR(IR));  // open: out_3
  Register #(.width(32)) register_2 (.D(br32_1_busa), .en(A), .Q(register_2_q), .clk(clk), .clr(rst));
  Register #(.width(32)) register_3 (.D({br32_1_busb, RAM}), .en(B), .Q(register_3_q), .clk(clk), .clr(rst));
  Comparator #(.width(32)) comparator_1 (.a(register_2_q), .b(register_3_q), .eq(comparator_1_eq));  // open: gt, lt
  Multiplexer #(.width(32), .enable("false")) multiplexer_4 (
    .in0(register_2_q), .in1(adder_1_out), .out(out_2), .sel(MUX3));
  Adder #(.width(32)) adder_1 (.a(register_2_q), .b(register_3_q), .out(adder_1_out));  // open: cin, cout
  Register #(.width(32)) register_4 (.D(out_2), .en(ALUout), .Q({register_4_q, ADD}), .clk(clk), .clr(rst));
  not not_1 (not_1_out, EN);
  RAM #(.addrWidth(16), .dataWidth(32), .bus("separate")) ram_1 (
    .addr(ADD), .din({br32_1_busb, RAM}), .data(ram_1_data), .str(clk), .ld(not_1_out));  // open: sel, clk, clr
  Register #(.width(32)) register_5 (.D(ram_1_data), .en(MDR), .Q(register_5_q), .clk(clk), .clr(rst));

  // Other names for the same wires on the sheet: MemWrite = EN; MUX2[1:0] = out_6; SEX[31:0] = out_5

  // Notes on the sheet:
  //   contents of rom_1 (hex, n*v repeats v):
  //   80000000 80180000 80200000 80080008 80100030 80200168 a2180060 44280000 24090000 25318000 2308c000
  //   a0000030 60300000 80380108 80480278 80580258 8067fff8 a63800d0 80400270 6c400000 6c480000 80500100
  //   6c500000 6c480000 6c580000 a00000e0 6c480000 6c580000 a00000e0
endmodule

module UC (
  input  [2:0] op,
  input  reloj,
  output [3:0] out_3,
  output PCload,
  output PCcount,
  output signal_branch,
  output MemWrite,
  output RegWrite,
  output MUX3,
  output [1:0] MUX2,
  output MUX1,
  output MDR,
  output ALUout,
  output B,
  output A,
  output IR
);

  wire [3:0] register_1_q;
  wire [15:14] rom_2_data;

  ROM #(.addrWidth(7), .dataWidth(4)) rom_1 (.addr({op, register_1_q}), .data(out_3));  // open: sel
  Register #(.width(4)) register_1 (.D(out_3), .Q(register_1_q), .clk(reloj));  // open: en, clr
  ROM #(.addrWidth(4), .dataWidth(16)) rom_2 (
    .addr(out_3),
    .data({rom_2_data, IR, A, B, ALUout, MDR, MUX1, MUX2, MUX3, RegWrite, MemWrite, signal_branch, PCcount, PCload}));  // open: sel

  // Notes on the sheet:
  //   contents of rom_1 (hex, n*v repeats v):
  //   1 15*0 1 2 6 13*0 1 3 0 7 0 0 0 9 8*0 1 4 0 0 8 11*0 1 a 14*0 1 5
  //   contents of rom_2 (hex, n*v repeats v):
  //   2000 1800 420 400 400 27 1b2 200 a 52 12
endmodule
