// Logisim project ejemplo uso tty.circ as structural Verilog: 1 circuit, main circuit main
module main (
  input  [6:0] in_1,
  input  in_2
);

  wire clk, tty_ctrl_1_clk2, tty_ctrl_1_clr, tty_ctrl_1_out;
  wire [6:0] tty_ctrl_1_dout;

  Clock clock_1 (.out(clk));
  tty_ctrl tty_ctrl_1 (
    .A({16{1'b1}}), .E(in_2), .out(tty_ctrl_1_out), .clr(tty_ctrl_1_clr), .D(in_1), .clk(clk),
    .Dout(tty_ctrl_1_dout), .clk2(tty_ctrl_1_clk2));
  TTY tty_1 (.data(tty_ctrl_1_dout), .clk(tty_ctrl_1_clk2), .we(tty_ctrl_1_out), .clr(tty_ctrl_1_clr));

  // Other names for the same wires on the sheet: D6_0[6:0] = in_1; en = in_2

  // Notes on the sheet:
  //   cte 0xffff
  //   permiso para imprimir en tty
  //   señal de reloj
  //   código ASCII 7 bits a imprimir en tty (0 borra pantalla)
endmodule
