// Logisim project tty-ctrl.circ as structural Verilog: 1 circuit, main circuit tty-ctrl
module tty_ctrl (
  input  clk,
  input  [15:0] A,
  input  E,
  input  [6:0] D,
  output clk2,
  output out,
  output clr,
  output [6:0] Dout
);

  wire and_2_out, and_3_out;

  and and_1 (out, A[0], A[1], A[2], A[3], A[4], A[5], A[6], A[7], A[8], A[9], A[10], A[11], A[12], A[13], A[14], A[15], E);
  and and_2 (and_2_out, ~D[0], ~D[1], ~D[2], ~D[3], ~D[4], ~D[5], ~D[6]);  // AND_Gate
  and and_3 (and_3_out, out, and_2_out);
  D_Flip_Flop d_ff_1 (.clk(clk), .D(and_3_out), .Q(clr), .en(1'b1));  // open: Qn, preset, reset

  assign clk2 = clk;
  assign Dout = D;
endmodule
