// Logisim project 755844-cache.circ as structural Verilog: 1 circuit, main circuit main
module main (
  output [31:0] inst
);

  wire and_1_out, and_2_out, and_3_out, and_5_out, clk, comparator_1_eq, comparator_2_eq, count_en,
       decoder_1_out0, decoder_1_out1, en_0, en_1, en_2, en_3, escritura, fifo_way, hit, hit_way, lectura,
       mem_en, not_1_out, not_2_out, not_3_out, not_4_out, not_5_out, not_8_out, not_9_out, not_10_out,
       not_11_out, ram_1_data, rst, x1, x2;
  wire [3:0] register_2_q, rom_1_data, word;
  wire [4:0] set;
  wire [6:0] tag;
  wire [7:0] counter_1_q, ram_2_data, ram_3_data;
  wire [31:0] bus, multiplexer_1_out, multiplexer_3_out, ram_4_data, ram_5_data, ram_6_data, ram_7_data,
       ram_8_data, ram_9_data, ram_10_data, ram_11_data, register_3_q, register_4_q, register_5_q,
       register_6_q;

  not not_1 (not_1_out, fifo_way);
  not not_2 (not_2_out, not_3_out);
  not not_3 (not_3_out, escritura);
  Counter counter_1 (.count(count_en), .Q(counter_1_q), .clk(clk), .clr(rst));  // open: load, D, carry
  RAM #(.addrWidth(5), .dataWidth(1), .bus("separate")) ram_1 (
    .addr(set), .din(not_1_out), .data(ram_1_data), .str(not_2_out), .clk(clk), .ld(not_3_out), .clr(rst));  // open: sel
  ROM #(.addrWidth(5), .dataWidth(4)) rom_1 (.addr({hit, register_2_q}), .data(rom_1_data));  // open: sel
  Clock clock_1 (.out(clk));
  Button button_1 (.out(rst));
  Register #(.width(1)) register_1 (.D(ram_1_data), .en(lectura), .Q(fifo_way), .clk(clk), .clr(rst));
  Register #(.width(4)) register_2 (.D(rom_1_data), .Q(register_2_q), .clk(clk), .clr(rst));  // open: en
  ROM #(.dataWidth(16)) rom_2 (.addr(counter_1_q), .data({tag, set, word}));  // open: sel
  not not_4 (not_4_out, x1);
  RAM #(.addrWidth(5), .bus("separate")) ram_2 (
    .addr(set), .din({tag, 1'b1}), .data(ram_2_data), .str(not_4_out), .clk(clk), .ld(x1), .clr(rst));  // open: sel
  ROM #(.addrWidth(4), .dataWidth(6)) rom_3 (
    .addr(register_2_q), .data({en_0, en_1, en_2, en_3, lectura, escritura}));  // open: sel
  MP_main main_1 (.dir({tag, set, word}), .mem_en(mem_en), .clk(clk), .dato(bus));
  not not_5 (not_5_out, x2);
  Comparator #(.width(7)) comparator_1 (.a(ram_2_data[7:1]), .b(tag), .eq(comparator_1_eq));  // open: gt, lt
  Decoder #(.enable("false")) decoder_1 (.out0(decoder_1_out0), .out1(decoder_1_out1), .sel(fifo_way));
  RAM #(.addrWidth(5), .bus("separate")) ram_3 (
    .addr(set), .din({tag, 1'b1}), .data(ram_3_data), .str(not_5_out), .clk(clk), .ld(x2), .clr(rst));  // open: sel
  and and_1 (and_1_out, ram_2_data[0], comparator_1_eq);
  Comparator #(.width(7)) comparator_2 (.a(ram_3_data[7:1]), .b(tag), .eq(comparator_2_eq));  // open: gt, lt
  or or_1 (hit, and_1_out, hit_way);
  and and_2 (and_2_out, escritura, decoder_1_out0);
  not not_6 (x1, and_2_out);
  and and_3 (and_3_out, decoder_1_out1, escritura);
  not not_7 (x2, and_3_out);
  and and_4 (hit_way, ram_3_data[0], comparator_2_eq);
  not not_8 (not_8_out, hit);
  and and_5 (and_5_out, not_8_out, lectura);
  not not_9 (not_9_out, lectura);
  Register #(.width(32)) register_3 (.D(bus), .en(en_0), .Q(register_3_q), .clk(clk), .clr(rst));
  and and_6 (count_en, hit, lectura);
  or or_2 (mem_en, and_5_out, not_9_out);
  Register #(.width(32)) register_4 (.D(bus), .en(en_1), .Q(register_4_q), .clk(clk), .clr(rst));
  not not_10 (not_10_out, x1);
  RAM #(.addrWidth(5), .dataWidth(32), .bus("separate")) ram_4 (
    .addr(set), .din(register_3_q), .data(ram_4_data), .str(not_10_out), .clk(clk), .ld(x1), .clr(rst));  // open: sel
  Register #(.width(32)) register_5 (.D(bus), .en(en_2), .Q(register_5_q), .clk(clk), .clr(rst));
  Register #(.width(32)) register_6 (.D(bus), .en(en_3), .Q(register_6_q), .clk(clk), .clr(rst));
  RAM #(.addrWidth(5), .dataWidth(32), .bus("separate")) ram_5 (
    .addr(set), .din(register_4_q), .data(ram_5_data), .str(not_10_out), .clk(clk), .ld(x1), .clr(rst));  // open: sel
  Multiplexer #(.select(2), .width(32), .enable("false")) multiplexer_1 (
    .in0(ram_4_data), .in1(ram_5_data), .in2(ram_6_data), .in3(ram_7_data), .out(multiplexer_1_out),
    .sel(word[3:2]));
  RAM #(.addrWidth(5), .dataWidth(32), .bus("separate")) ram_6 (
    .addr(set), .din(register_5_q), .data(ram_6_data), .str(not_10_out), .clk(clk), .ld(x1), .clr(rst));  // open: sel
  RAM #(.addrWidth(5), .dataWidth(32), .bus("separate")) ram_7 (
    .addr(set), .din(register_6_q), .data(ram_7_data), .str(not_10_out), .clk(clk), .ld(x1), .clr(rst));  // open: sel
  Multiplexer #(.width(32), .enable("false")) multiplexer_2 (
    .in0(multiplexer_1_out), .in1(multiplexer_3_out), .out(inst), .sel(hit_way));
  not not_11 (not_11_out, x2);
  RAM #(.addrWidth(5), .dataWidth(32), .bus("separate")) ram_8 (
    .addr(set), .din(register_3_q), .data(ram_8_data), .str(not_11_out), .clk(clk), .ld(x2), .clr(rst));  // open: sel
  RAM #(.addrWidth(5), .dataWidth(32), .bus("separate")) ram_9 (
    .addr(set), .din(register_4_q), .data(ram_9_data), .str(not_11_out), .clk(clk), .ld(x2), .clr(rst));  // open: sel
  Multiplexer #(.select(2), .width(32), .enable("false")) multiplexer_3 (
    .in0(ram_8_data), .in1(ram_9_data), .in2(ram_10_data), .in3(ram_11_data), .out(multiplexer_3_out),
    .sel(word[3:2]));
  RAM #(.addrWidth(5), .dataWidth(32), .bus("separate")) ram_10 (
    .addr(set), .din(register_5_q), .data(ram_10_data), .str(not_11_out), .clk(clk), .ld(x2), .clr(rst));  // open: sel
  RAM #(.addrWidth(5), .dataWidth(32), .bus("separate")) ram_11 (
    .addr(set), .din(register_6_q), .data(ram_11_data), .str(not_11_out), .clk(clk), .ld(x2), .clr(rst));  // open: sel

  // Notes on the sheet:
  //   contents of rom_1 (hex, n*v repeats v):
  //   1 2 3 4 5 6 7 8 9 a b c 5*0 2 3 4 5 6 7 8 9 a b c
  //   contents of rom_2 (hex, n*v repeats v):
  //   2000 4000 8000 8004 2140 4140 8140 8144 6204 d800 f808 d804
  //   contents of rom_3 (hex, n*v repeats v):
  //   2 0 0 0 20 0 10 0 8 0 4 1 2
endmodule
